// Logisim project WriteControl.circ as structural Verilog: 1 circuit, main circuit main
module main (
  input  PIN11,
  input  A12,
  input  A13,
  input  A14,
  input  A15,
  input  PIN7,
  output WRITE__ACTIVE_LOW
);

  wire d_ff_1_q, nand_1_out, nand_2_out, nand_3_out, nor_1_out, nor_2_out, nor_3_out, not_1_out, not_2_out,
       not_3_out, not_4_out, not_5_out, not_6_out, not_7_out, not_8_out, P36_CLK_out;

  Clock P36_CLK (.out(P36_CLK_out));
  not not_1 (not_1_out, P36_CLK_out);
  not not_2 (not_2_out, not_7_out);
  not not_3 (not_3_out, not_2_out);
  not not_4 (not_4_out, not_3_out);
  nor nor_1 (nor_1_out, A12, A13);
  nor nor_2 (nor_2_out, A14, A15);
  not not_5 (not_5_out, not_6_out);
  not not_6 (not_6_out, not_1_out);
  not not_7 (not_7_out, not_5_out);
  nand nand_1 (nand_1_out, nor_1_out, nor_2_out);
  nor nor_3 (nor_3_out, nand_3_out, PIN7);
  not not_8 (not_8_out, nand_2_out);
  nand nand_2 (nand_2_out, PIN11, nand_1_out);
  not nand_3 (nand_3_out, nand_1_out);  // NAND_Gate
  D_Flip_Flop d_ff_1 (.clk(not_4_out), .D(nor_3_out), .Q(d_ff_1_q));  // open: Qn, preset, en, reset
  nand nand_4 (WRITE__ACTIVE_LOW, not_8_out, d_ff_1_q);
  nand nand_5 (WRITE__ACTIVE_LOW, not_8_out, d_ff_1_q);
  nand nand_6 (WRITE__ACTIVE_LOW, not_8_out, d_ff_1_q);
  nand nand_7 (WRITE__ACTIVE_LOW, not_8_out, d_ff_1_q);
  // NAND_Gate nand_8 has open pins: in0=not_8_out, out=open
endmodule
